# Fritzing sketch devre tasarimi (saved by Fritzing 0.9.3b)
breadboards: 1

parts:
  Raspberry_Pi_1 = Raspberry Pi 3 [part_number=RPI-3-V1.2]
  U1 = MLX90614 [package=to-39]
  LED5 = RGB LED - (4 legs) [package="5 mm [THT]"]
  R1 = Resistor [tolerance=±5% resistance=220 package="2512 [SMD]"]
  R2 = Resistor [tolerance=±5% resistance=220 package="2512 [SMD]"]
  R3 = Resistor [tolerance=±5% resistance=220 package="2512 [SMD]"]
  U3 = TRANSCHIPTC5747 [package=camera_sfv24r-2st_2]  # not connected

nets:
  N1: Raspberry_Pi_1.GPIO2, U1.SCL_VZ
  N2: Raspberry_Pi_1.GPIO3, U1.PWM_SDA
  N3: Raspberry_Pi_1.GIPO17, R1.Pin_0
  N4: Raspberry_Pi_1.GIPO27, R2.Pin_0
  N5: Raspberry_Pi_1.GIPO22, R3.Pin_0
  N6: Raspberry_Pi_1.GND, LED5.red_cathode
  N7: LED5.common_anode, R1.Pin_1
  N8: LED5.green_cathode, R2.Pin_1
  N9: LED5.blue_cathode, R3.Pin_1

notes:
  Pi Camera
  IR Termometer Sensor
  Raspberry Pi 4
  CLI CABLE
